// Logisim project cpu32.circ as structural Verilog: 8 circuits, main circuit ALU
module InstructionDecode (
  input  [31:0] Instruction,
  output [5:0] op,
  output [4:0] rs,
  output [4:0] rt,
  output [4:0] rd,
  output [4:0] shamt,
  output [5:0] funct,
  output [15:0] immediate,
  output [25:0] address
);


  assign address = Instruction[25:0];
  assign funct = Instruction[5:0];
  assign immediate = Instruction[15:0];
  assign op = Instruction[31:26];
  assign rd = Instruction[15:11];
  assign rs = Instruction[25:21];
  assign rt = Instruction[20:16];
  assign shamt = Instruction[10:6];

  // Notes on the sheet:
  //   J-type
  //   I-type
  //   R-type
endmodule

module Registers (
  input  [4:0] ReadRegister1,
  input  [4:0] ReadRegister2,
  input  [4:0] WriteRegister,
  input  [31:0] WriteData,
  input  Write,
  input  Clear,
  output [31:0] ReadData1,
  output [31:0] ReadData2
);

  wire demultiplexer_1_out0, demultiplexer_1_out1, demultiplexer_1_out2, demultiplexer_1_out3,
       demultiplexer_1_out4, demultiplexer_1_out5, demultiplexer_1_out6, demultiplexer_1_out7;
  wire [31:0] registers4_1_p7, registers4_1_p8, registers4_2_p7, registers4_2_p8, registers4_3_p7,
       registers4_3_p8, registers4_4_p7, registers4_4_p8, registers4_5_p7, registers4_5_p8, registers4_6_p7,
       registers4_6_p8, registers4_7_p7, registers4_7_p8, registers4z_1_p7, registers4z_1_p8;

  Demultiplexer #(.select(3), .width(1), .tristate("false")) demultiplexer_1 (
    .out0(demultiplexer_1_out0), .out1(demultiplexer_1_out1), .out2(demultiplexer_1_out2),
    .out3(demultiplexer_1_out3), .out4(demultiplexer_1_out4), .out5(demultiplexer_1_out5),
    .out6(demultiplexer_1_out6), .out7(demultiplexer_1_out7), .in(Write), .sel(WriteRegister[4:2]));
  // Registers4Z registers4z_1: pin names not known; wires that end beside it: ReadRegister1[1:0], ReadRegister2[1:0], WriteRegister[1:0], WriteData, demultiplexer_1_out0, Clear, registers4z_1_p7, registers4z_1_p8
  // Registers4 registers4_1: pin names not known; wires that end beside it: ReadRegister1[1:0], ReadRegister2[1:0], WriteRegister[1:0], WriteData, demultiplexer_1_out1, Clear, registers4_1_p7, registers4_1_p8
  // Registers4 registers4_2: pin names not known; wires that end beside it: ReadRegister1[1:0], ReadRegister2[1:0], WriteRegister[1:0], WriteData, demultiplexer_1_out2, Clear, registers4_2_p7, registers4_2_p8
  // Registers4 registers4_3: pin names not known; wires that end beside it: ReadRegister1[1:0], ReadRegister2[1:0], WriteRegister[1:0], WriteData, demultiplexer_1_out3, Clear, registers4_3_p7, registers4_3_p8
  // Registers4 registers4_4: pin names not known; wires that end beside it: ReadRegister1[1:0], ReadRegister2[1:0], WriteRegister[1:0], WriteData, demultiplexer_1_out4, Clear, registers4_4_p7, registers4_4_p8
  // Registers4 registers4_5: pin names not known; wires that end beside it: ReadRegister1[1:0], ReadRegister2[1:0], WriteRegister[1:0], WriteData, demultiplexer_1_out5, Clear, registers4_5_p7, registers4_5_p8
  // Registers4 registers4_6: pin names not known; wires that end beside it: ReadRegister1[1:0], ReadRegister2[1:0], WriteRegister[1:0], WriteData, demultiplexer_1_out6, Clear, registers4_6_p7, registers4_6_p8
  // Registers4 registers4_7: pin names not known; wires that end beside it: ReadRegister1[1:0], ReadRegister2[1:0], WriteRegister[1:0], WriteData, demultiplexer_1_out7, Clear, registers4_7_p7, registers4_7_p8
  Multiplexer #(.select(3), .width(32)) multiplexer_1 (
    .in0(registers4z_1_p7), .in1(registers4_1_p7), .in2(registers4_2_p7), .in3(registers4_3_p7),
    .in4(registers4_4_p7), .in5(registers4_5_p7), .in6(registers4_6_p7), .in7(registers4_7_p7),
    .out(ReadData1), .sel(ReadRegister1[4:2]));
  Multiplexer #(.select(3), .width(32)) multiplexer_2 (
    .in0(registers4z_1_p8), .in1(registers4_1_p8), .in2(registers4_2_p8), .in3(registers4_3_p8),
    .in4(registers4_4_p8), .in5(registers4_5_p8), .in6(registers4_6_p8), .in7(registers4_7_p8),
    .out(ReadData2), .sel(ReadRegister2[4:2]));
endmodule

module SignExtend (
  input  [15:0] in_1,
  output [31:0] out_2
);


  assign out_2 = {{17{in_1[15]}}, in_1[14:0]};
endmodule

module ALU (
  input  [31:0] A,
  input  [31:0] B,
  input  [3:0] Operation,
  output Zero,
  output [31:0] Result,
  output Overflow
);

  wire getsign_1_p2, getsign_2_p2, overflow_1_p3, xor_1_out;
  wire [31:0] adder_1_out, and_1_out, getsign_1_p3, getsign_2_p3, getsign_3_p3, multiplexer_1_out,
       multiplexer_2_out, not_1_out, not_2_out, or_1_out, setlsb_1_p3;

  assign not_1_out = ~A;  // NOT_Gate not_1, 32 bits wide
  assign not_2_out = ~B;  // NOT_Gate not_2, 32 bits wide
  Multiplexer #(.select(1), .width(32)) multiplexer_1 (
    .in0(A), .in1(not_1_out), .out(multiplexer_1_out), .sel(Operation[3]));
  Multiplexer #(.select(1), .width(32)) multiplexer_2 (
    .in0(B), .in1(not_2_out), .out(multiplexer_2_out), .sel(Operation[2]));
  // GetSign getsign_1: pin names not known; wires that end beside it: multiplexer_1_out, getsign_1_p2, getsign_1_p3
  // GetSign getsign_2: pin names not known; wires that end beside it: multiplexer_2_out, getsign_2_p2, getsign_2_p3
  // Overflow overflow_1: pin names not known; wires that end beside it: getsign_1_p2, getsign_2_p2, overflow_1_p3, Operation[1:0], Overflow
  assign and_1_out = getsign_1_p3 & getsign_2_p3;  // AND_Gate and_1, 32 bits wide
  assign or_1_out = getsign_1_p3 | getsign_2_p3;  // OR_Gate or_1, 32 bits wide
  Adder #(.width(32)) adder_1 (
    .a(getsign_1_p3), .b(getsign_2_p3), .out(adder_1_out), .cin(Operation[2]));  // open: cout
  // GetSign getsign_3: pin names not known; wires that end beside it: adder_1_out, overflow_1_p3, getsign_3_p3
  xor xor_1 (xor_1_out, overflow_1_p3, Overflow);
  // SetLSB setlsb_1: pin names not known; wires that end beside it: {32{1'b0}}, xor_1_out, setlsb_1_p3
  Multiplexer #(.select(2), .width(32)) multiplexer_3 (
    .in0(and_1_out), .in1(or_1_out), .in2(getsign_3_p3), .in3(setlsb_1_p3), .out(Result), .sel(Operation[1:0]));
  // Zero zero_1: pin names not known; wires that end beside it: Result, Zero

  // Notes on the sheet:
  //   +/-
  //   +/-
  //   +/-
  //   LSB
  //   0?
endmodule

module BranchAddress (
  input  [31:0] PC_4,
  input  [31:0] Address,
  output [31:0] BranchAddress
);

  Adder #(.width(32)) adder_1 (.a(PC_4), .b({Address[29:0], 2'b00}), .out(BranchAddress));  // open: cin, cout
endmodule

module JumpAddress (
  input  [25:0] Address,
  input  [31:0] PC_4,
  output [31:0] JumpAddress
);


  assign JumpAddress = {PC_4[31:28], Address, 2'b00};
endmodule

module Control (
  input  [5:0] op,
  output RegDst,
  output Branch,
  output MemRead,
  output MemToReg,
  output [1:0] ALUop,
  output MemWrite,
  output ALUsrc,
  output RegWrite
);

  Control_0 control_0_1 (
    .op_5(op[5]), .op_4(op[4]), .op_3(op[3]), .op_2(op[2]), .op_1(op[1]), .op_0(op[0]), .RegDst(RegDst),
    .Branch(Branch), .MemRead(MemRead), .MemToReg(MemToReg), .MemWrite(MemWrite), .ALUsrc(ALUsrc),
    .RegWrite(RegWrite));
  Control_1 control_1_1 (
    .op_5(op[5]), .op_4(op[4]), .op_3(op[3]), .op_2(op[2]), .op_1(op[1]), .op_0(op[0]), .ALUop_1(ALUop[1]),
    .ALUop_0(ALUop[0]));
endmodule

module ALUcontrol (
  input  [5:0] funct,
  input  [1:0] ALUop,
  output [3:0] Operation
);

  ALUcontrol_0 alucontrol_0_1 (
    .ALUop_1(ALUop[1]), .ALUop_0(ALUop[0]), .F5(funct[5]), .F4(funct[4]), .F3(funct[3]), .F2(funct[2]),
    .F1(funct[1]), .F0(funct[0]), .Operation_3(Operation[3]), .Operation_2(Operation[2]),
    .Operation_1(Operation[1]), .Operation_0(Operation[0]));
endmodule
