// Logisim project datapath_automatico.circ as structural Verilog: 4 circuits, main circuit Datapath
module Datapath (
  input  Reset,
  input  Clear,
  input  Clear_2,
  output [4:0] Shamt
);

  wire alu_1_zero, and_1_out, Clock_out, control_1_branch, control_1_escrevemem, control_1_escrevereg,
       control_1_lemem, control_1_memparareg, control_1_origalu, control_1_regdst, not_1_out,
       wordaddress_1_p2, wordaddress_2_p2;
  wire [1:0] control_1_opalu;
  wire [3:0] alucontrol_1_operation;
  wire [4:0] instructiondecode_1_rd, instructiondecode_1_rs, instructiondecode_1_rt, multiplexer_1_out;
  wire [5:0] instructiondecode_1_funct, instructiondecode_1_op;
  wire [15:0] instructiondecode_1_immediate;
  wire [31:0] adder_1_out, branchaddress_1_branchaddress, mips_ram_1_p4, mips_ram_2_p4, multiplexer_2_out,
       multiplexer_3_out, registerfile_1_p1, registerfile_1_p7, registerfile_1_p8, shifter_1_out,
       signextend_1_out_2, wordaddress_1_p1, wordaddress_2_p1;

  // WordAddress wordaddress_1: pin names not known; wires that end beside it: wordaddress_1_p1, wordaddress_1_p2, wordaddress_1_p2, 1'b0, 4'b1111
  Register #(.width(32)) register_1 (
    .D(multiplexer_3_out), .Q(wordaddress_1_p1), .clk(Clock_out), .clr(Reset));  // open: en
  Clock Clock (.out(Clock_out));
  // MIPS_RAM mips_ram_1: pin names not known; wires that end beside it: 1'b0, 1'b1, Clear, mips_ram_1_p4
  Adder #(.width(32)) adder_1 (.a(32'h4), .b(wordaddress_1_p1), .out(adder_1_out));  // open: cin, cout
  InstructionDecode instructiondecode_1 (
    .Instruction(mips_ram_1_p4), .op(instructiondecode_1_op), .rs(instructiondecode_1_rs),
    .rt(instructiondecode_1_rt), .rd(instructiondecode_1_rd), .shamt(Shamt),
    .funct(instructiondecode_1_funct), .immediate(instructiondecode_1_immediate));  // open: address
  Control control_1 (
    .op(instructiondecode_1_op), .RegDst(control_1_regdst), .Branch(control_1_branch),
    .LeMem(control_1_lemem), .MemparaReg(control_1_memparareg), .OpALU(control_1_opalu),
    .EscreveMem(control_1_escrevemem), .OrigALU(control_1_origalu), .EscreveReg(control_1_escrevereg));
  Multiplexer #(.width(5), .enable("false")) multiplexer_1 (
    .in0(instructiondecode_1_rt), .in1(instructiondecode_1_rd), .out(multiplexer_1_out),
    .sel(control_1_regdst));
  not not_1 (not_1_out, Clock_out);
  SignExtend signextend_1 (.in_1(instructiondecode_1_immediate), .out_2(signextend_1_out_2));
  // RegisterFile registerfile_1: pin names not known; wires that end beside it: registerfile_1_p1, not_1_out, control_1_escrevereg, multiplexer_1_out, instructiondecode_1_rs, instructiondecode_1_rt, registerfile_1_p7, registerfile_1_p8
  Multiplexer #(.width(32), .enable("false")) multiplexer_2 (
    .in0(registerfile_1_p8), .in1(signextend_1_out_2), .out(multiplexer_2_out), .sel(control_1_origalu));
  // WordAddress wordaddress_2: pin names not known; wires that end beside it: wordaddress_2_p1, wordaddress_2_p2, wordaddress_2_p2, registerfile_1_p8, control_1_escrevemem, 4'b1111
  Shifter #(.width(32)) shifter_1 (.in(signextend_1_out_2), .\dist (5'b00010), .out(shifter_1_out));
  ALUcontrol alucontrol_1 (
    .Funct(instructiondecode_1_funct), .OpALU(control_1_opalu), .Operation(alucontrol_1_operation));
  Multiplexer #(.width(32), .enable("false")) multiplexer_3 (
    .in0(adder_1_out), .in1(branchaddress_1_branchaddress), .out(multiplexer_3_out), .sel(and_1_out));
  BranchAddress branchaddress_1 (
    .PC_4(adder_1_out), .Address(shifter_1_out), .BranchAddress(branchaddress_1_branchaddress));
  and and_1 (and_1_out, control_1_branch, alu_1_zero);
  ALU alu_1 (
    .A(registerfile_1_p7), .B(multiplexer_2_out), .Operation(alucontrol_1_operation), .Zero(alu_1_zero),
    .Result(wordaddress_2_p1));  // open: Overflow
  // MIPS_RAM mips_ram_2: pin names not known; wires that end beside it: not_1_out, control_1_lemem, Clear_2, mips_ram_2_p4
  Multiplexer #(.width(32), .enable("false")) multiplexer_4 (
    .in0(wordaddress_2_p1), .in1(mips_ram_2_p4), .out(registerfile_1_p1), .sel(control_1_memparareg));

  // Notes on the sheet:
  //   Opcode
  //   8c0a0000
  //   8c0b0004
  //   014b4820
  //   ac090008
  //   1000ffff
  //   PC
  //   Memória de Instruções
  //   Instruções
  //   Decodificador
  //   main:  lw $t2, 0($zero) 
  //   lw $t3, 4($zero)
  //   add $t1, $t2, $t3
  //   sw $t1, 8($zero)
  //   exit:  beq $zero, $zero, exit
  //   Controle
  //   Controle
  //   lw    001100011
  //   lw    001100011
  //   R     100010001
  //   sw    X00X00110
  //   beq   X10X01000
  //   Registradores
  //   Extensão
  //   Controle ALU
  //   0010 add
  //   0010 add
  //   0010 add
  //   0010 add
  //   0110 sub
  //   ALU
  //   Memória de Dados
  //   Branch
endmodule

module Control (
  input  [5:0] op,
  output RegDst,
  output Branch,
  output LeMem,
  output MemparaReg,
  output [1:0] OpALU,
  output EscreveMem,
  output OrigALU,
  output EscreveReg
);

  Decod_control decod_control_1 (
    .Opcode(op), ._0___R(OpALU[1]), ._4___BEQ(Branch), ._35___LW(LeMem), ._43___SW(EscreveMem));
  or or_1 (OrigALU, EscreveMem, LeMem);
  or or_2 (EscreveReg, LeMem, OpALU[1]);

  assign MemparaReg = LeMem;
  assign OpALU[0] = Branch;
  assign RegDst = OpALU[1];
endmodule

module ALUcontrol (
  input  [5:0] Funct,
  input  [1:0] OpALU,
  output [3:0] Operation
);

  wire and_2_out, or_1_out;

  or or_1 (or_1_out, Funct[0], Funct[3]);
  and and_1 (Operation[0], or_1_out, OpALU[1]);
  and and_2 (and_2_out, Funct[1], OpALU[1]);
  or or_2 (Operation[1], ~OpALU[1], ~Funct[2]);  // OR_Gate
  or or_3 (Operation[2], and_2_out, OpALU[0]);

  assign Operation[3] = 1'b0;
endmodule

module Decod_control (
  input  [5:0] Opcode,
  output _0___R,
  output _4___BEQ,
  output _35___LW,
  output _43___SW
);

  and and_1 (_0___R, ~Opcode[5], ~Opcode[4], ~Opcode[3], ~Opcode[2], ~Opcode[1], ~Opcode[0]);  // AND_Gate
  and and_2 (_4___BEQ, ~Opcode[5], ~Opcode[4], ~Opcode[3], Opcode[2], ~Opcode[1], ~Opcode[0]);  // AND_Gate
  and and_3 (_35___LW, Opcode[5], ~Opcode[4], ~Opcode[3], ~Opcode[2], Opcode[1], Opcode[0]);  // AND_Gate
  and and_4 (_43___SW, Opcode[5], ~Opcode[4], Opcode[3], ~Opcode[2], Opcode[1], Opcode[0]);  // AND_Gate
endmodule
